# Fritzing sketch 3.3V-5V_Supply_ケース内配線 (saved by Fritzing 0.9.2b)
perfboards: 1

parts:
  J1 = female pin header, 2 pins [form="♀ (female)"]
  J2 = female pin header, 3 pins [form="♀ (female)"]
  Power_plug1 = Power plug
  Power_plug2 = Power plug
  Power_plug3 = Power plug
  Power_plug4 = Power plug
  S1 = Toggle Switch [package=THT]

nets:
  N1: J1.pin1, S1.COM
  N2: J1.pin2, Power_plug1.GND
  GND: J2.pin1, Power_plug2.GND, Power_plug3.GND
  N3: J2.pin2, Power_plug4.GND
  VCC: J2.pin3, Power_plug2.VCC, Power_plug3.VCC, Power_plug4.VCC
  N4: Power_plug1.VCC, S1.L1

notes:
  3.3V-5V Power Supply
  5V
  3.3V
  GND
  9V
  GND
